# Fritzing sketch Covid Sarthi (saved by Fritzing 0.9.3b)

parts:
  Part1 = Arduino Uno (Rev3)
  LCD1 = LCD screen
  RHT1 = Humidity and Temperature Sensor RHT03
  J1 = Infrared Proximity Sensor
  LED1 = smd LED [color="Red (633nm)" package="1206 [SMD]"]
  R1 = Resistor [tolerance=±5% resistance=220 package="0603 [SMD]"]
  J2 = Piezo Speaker

nets:
  N1: Part1.D8, LCD1.V0
  N2: Part1.D9_PWM, R1.Pin_1, J2.pin2
  N3: Part1.D10_PWM/SS, J1.Vout
  N4: Part1.D13/SCK, RHT1.Vcc
  GND: Part1.GND, LCD1.VSS, RHT1.GND_2, J1.GND, LED1.cathode
  N5: Part1.D1/TX, LCD1.RS
  N6: Part1.D2, LCD1.E
  N7: Part1.D4, LCD1.DB4
  N8: Part1.D5_PWM, LCD1.DB5
  N9: Part1.D6_PWM, LCD1.DB6
  N10: Part1.D7, LCD1.DB7
